// Logisim project pulsweite.circ as structural Verilog: 1 circuit, main circuit main
module main (
  input  in_1,
  input  in_2,
  input  in_3,
  input  in_4,
  input  in_5,
  input  in_6,
  input  NR1,
  input  R2,
  input  NS3,
  input  S1,
  input  S2,
  input  NR3,
  input  in_13,
  input  in_14,
  output out_15,
  output out_16,
  output out_17,
  output out_18,
  output out_19,
  output out_20,
  output out_21,
  output out_22,
  output out_23,
  output out_24
);

  wire not_1_out;

  or or_1 (out_17, in_3, in_6);
  and and_1 (out_18, NR1, out_21);
  or or_2 (out_21, out_18, S1);
  not not_1 (not_1_out, in_14);
  nand nand_1 (out_24, in_13, not_1_out);
  and and_2 (out_15, in_1, in_4);
  nor nor_1 (out_19, R2, out_22);
  nor nor_2 (out_22, out_19, S2);
  nand nand_2 (out_16, in_2, in_5);
  nand nand_3 (out_20, NS3, out_23);
  nand nand_4 (out_23, out_20, NR3);
endmodule
